# Fritzing sketch globe_board (saved by Fritzing 0.7.10b)
stripboards: 1

parts:
  U1 = atmega168 [package=dip]
  R1 = Resistor [tolerance=±5% resistance=100 package=THT]
  J4 = female alternating pin header, 2 pins [form="♀ (female)"]
  LED1 = LED - 3mm [color="Infrared (940nm)" package="3 mm [THT]"]
  S1 = Pushbutton [package="[THT]"]
  S2 = Pushbutton [package="[THT]"]
  S3 = Pushbutton [package="[THT]"]
  S4 = Pushbutton [package="[THT]"]
  S5 = Pushbutton [package="[THT]"]
  S6 = Pushbutton [package="[THT]"]

nets:
  N1: U1.D2, J4.pin2, LED1.anode
  N2: U1.GND#7, R1.Pin_0, S1.Pin_1, S1.Pin_2, S2.Pin_1, S2.Pin_2, S3.Pin_1, S3.Pin_2, S4.Pin_1, S4.Pin_2, S5.Pin_1, S5.Pin_2, S6.Pin_1, S6.Pin_2
  N3: R1.Pin_1, J4.pin1, LED1.cathode

notes:
  Europe
  Africa
  Asia
  North America
  South America
  Australia
